# Fritzing sketch schema (saved by Fritzing 0.9.2b)
breadboards: 1

parts:
  Bauteil1 = Arduino Uno (Rev3)
  Bauteil2 = Humidity Sensor - HIH-4030 Breakout
  M1 = DC Motor
  LED1 = LED - 5mm [color="Red (633nm)" package="5 mm [THT]"]

nets:
  N1: Bauteil1.D12/MISO, M1.pin_2
  N2: Bauteil1.D13/SCK, Bauteil2.VCC, LED1.cathode
  GND: Bauteil1.GND, Bauteil2.GND, M1.pin_1, LED1.anode
